# Fritzing sketch atelier_moisture_secondaire (saved by Fritzing 0.9.10b)
breadboards: 1

parts:
  Part1 = Arduino Mega 2560 (Rev3)
  LED1 = LEDs [package=led10mm]
  R1 = Resistor [tolerance=±5% resistance=220 package="2010 [SMD]"]
  Part2 = Soil Moisture Sensor

nets:
  N1: Part1.A0, Part2.SIG
  GND: Part1.GND, LED1.C, Part2.GND
  N2: Part1.D2_PWM, Part2.VCC
  N3: Part1.D4_PWM, R1.Pin_1
  N4: LED1.A, R1.Pin_0
