# Fritzing sketch branchement_bouton (saved by Fritzing 0.9.9b)
breadboards: 1

parts:
  Part1 = Arduino Mega 2560 (Rev3)
  Part2 = Breadboard Power Supply Board SMD
  LED1 = smd LED [color="Red (633nm)" package="0805 [SMD]"]
  R1 = Resistor [tolerance=±5% power=0.25 resistance=220 package=THT]
  S1 = Pushbutton [package="[THT]"]

nets:
  GND: Part1.GND, Part2.GND, LED1.cathode, S1.Pin_3, S1.Pin_4
  N1: Part1.D9_PWM, R1.Pin_1
  N2: Part1.D2_PWM, S1.Pin_1, S1.Pin_2
  N3: LED1.anode, R1.Pin_0
