# Fritzing sketch branchement_led (saved by Fritzing 0.9.9b)
breadboards: 1

parts:
  Part1 = Arduino Mega 2560 (Rev3)
  Part2 = Breadboard Power Supply Board SMD
  LED1 = smd LED [color="Red (633nm)" package="0805 [SMD]"]
  R1 = Resistor [tolerance=±5% power=0.25 resistance=220 package=THT]

nets:
  GND: Part1.GND, Part2.GND, LED1.cathode
  N1: Part1.D9_PWM, R1.Pin_1
  N2: LED1.anode, R1.Pin_0
