# Fritzing sketch branchement_psu (saved by Fritzing 0.9.10b)
breadboards: 1

parts:
  Part1 = Arduino Mega 2560 (Rev3)
  Part3 = Breadboard Power Supply Board SMD

nets:
  GND: Part1.GND, Part3.GND
  5V: Part1.5V, Part3.VCC
