# Fritzing sketch breadboard_psu (saved by Fritzing 1.0.4)
breadboards: 1

parts:
  Part1 = Arduino Mega 2560 (Rev3)
  R1 = PHOTOCELL [package=photocell-kit]
  R2 = Resistor [tolerance=±5% power=0.25W resistance=4.7k package=THT]
  LED1 = LED - 5mm [color="Red (633nm)" current=0.030A package="5 mm [THT]"]
  LED2 = LED - 5mm [color="Blue (470nm)" current=0.030A package="5 mm [THT]"]
  R3 = Resistor [tolerance=±5% power=0.25W resistance=330 package=THT]
  R4 = Resistor [tolerance=±5% power=0.25W resistance=330 package=THT]
  S1 = Pushbutton [package="[THT]"]
  YwRobot_Power_Supply1 = YwRobot Breadboard Power Supply [part_number=545043]
  M1 = Dagu DGServo 9g (Top view) [part_number=RS001B]

nets:
  N1: Part1.A0, R1.P$2, R2.Pin_0
  GND: Part1.GND, R2.Pin_1, R3.Pin_1, R4.Pin_1, S1.Pin_3, S1.Pin_4, YwRobot_Power_Supply1.GND#13, YwRobot_Power_Supply1.GND#14, M1.gnd
  N2: Part1.D9_PWM, LED1.anode
  N3: Part1.D8_PWM, LED2.anode
  N4: Part1.D2_PWM, S1.Pin_1, S1.Pin_2
  N5: Part1.D44, M1.pulse
  N6: R1.P$1, YwRobot_Power_Supply1.VCC#9, YwRobot_Power_Supply1.VCC#10, M1.vcc
  N7: LED1.cathode, R4.Pin_0
  N8: LED2.cathode, R3.Pin_0
  N9: YwRobot_Power_Supply1.VCC#5, YwRobot_Power_Supply1.VCC#6
  N10: YwRobot_Power_Supply1.GND#11, YwRobot_Power_Supply1.GND#12

custom parts:
  YwRobot Breadboard Power Supply: The YwRobot Breadboard Power Supply (MB-V2) has two power rails; they can be 5V or 3V3. Power to the module can be provided through the female USB socket or through the A10 (female) 2.1mm power jack.
