# Fritzing sketch dht11 (saved by Fritzing 0.9.9b)
breadboards: 1

parts:
  Part1 = Arduino Mega 2560 (Rev3)
  Part2 = Breadboard Power Supply Board SMD
  J2 = male pin header, 3 pins [form="♂ (male)"]

nets:
  GND: Part1.GND, Part2.GND, J2.pin1
  5V: Part1.5V, Part2.VCC, J2.pin3
  N1: Part1.D2_PWM, J2.pin2
