# Fritzing sketch l293d (saved by Fritzing 0.9.10b)
breadboards: 1

parts:
  Part1 = Arduino Mega 2560 (Rev3)
  Part2 = Breadboard Power Supply Board SMD
  M1 = DC Motor [voltage_(max)=6V voltage_(min)=3V]
  IC1 = L293D [package=THT]

nets:
  GND: Part1.GND, Part2.GND, IC1.+V
  N1: Part1.D23, IC1.In_1
  N2: Part1.D25, IC1.In_2
  N3: Part2.VCC, IC1.Enable_1, IC1.0V, IC1.+Vmotor
  N4: M1.pin_1, IC1.Out_2_(_Controlled_by_Enable_1_)
  N5: M1.pin_2, IC1.Out_1_(_Controlled_by_Enable_1_)
