# Fritzing sketch mpu6050 (saved by Fritzing 0.9.9b)
breadboards: 1

parts:
  Part1 = Arduino Mega 2560 (Rev3)
  Part2 = InvenSense MPU6050

nets:
  N1: Part1.D21/SCL, Part2.SCL
  N2: Part1.D20/SDA, Part2.SDA
  GND: Part1.GND, Part2.GND
  5V: Part1.5V, Part2.VCC
