# Fritzing sketch photoresistance (saved by Fritzing 0.9.9b)
breadboards: 1

parts:
  Part1 = Arduino Mega 2560 (Rev3)
  Part2 = Breadboard Power Supply Board SMD
  R1 = PHOTOCELL [package=photocell-kit]
  R2 = Resistor [tolerance=±5% power=0.25 resistance=10k package=THT]

nets:
  N1: Part1.A0, Part1.5V, R1.P$1
  GND: Part1.GND, Part2.GND, R2.Pin_1
  N2: R1.P$2, R2.Pin_0
