# Fritzing sketch resistance_rappel (saved by Fritzing 0.9.9b)
breadboards: 1

parts:
  Part1 = Arduino Mega 2560 (Rev3)
  S1 = Pushbutton [package="[THT]"]
  R1 = Resistor [tolerance=±5% power=0.25 resistance=220 package=THT]

nets:
  N1: Part1.GND, R1.Pin_1
  GND: Part1.5V, S1.Pin_1, S1.Pin_2
  N2: Part1.D2_PWM, S1.Pin_3, S1.Pin_4, R1.Pin_0
