# Fritzing sketch resistance_tirage (saved by Fritzing 0.9.10b)
breadboards: 1

parts:
  Part1 = Arduino Mega 2560 (Rev3)
  S1 = Pushbutton [package="[THT]"]
  R1 = Resistor [tolerance=±5% power=0.25 resistance=220 package=THT]

nets:
  GND: Part1.GND, S1.Pin_1, S1.Pin_2
  N1: Part1.5V, R1.Pin_1
  N2: Part1.D2_PWM, S1.Pin_3, S1.Pin_4, R1.Pin_0
