# Fritzing sketch branchement_servo (saved by Fritzing 0.9.9b)
breadboards: 1

parts:
  Part1 = Arduino Mega 2560 (Rev3)
  J1 = Basic Servo
  Part2 = Breadboard Power Supply Board SMD

nets:
  GND: Part1.GND, J1.gnd, Part2.GND
  N1: Part1.D3_PWM, J1.pulse
  VCC: J1.vcc, Part2.VCC
